# Fritzing sketch node (saved by Fritzing 0.9.3b)
breadboards: 1

parts:
  Microcontroller = Arduino Uno (Rev3)
  C1 = Electrolytic Capacitor [capacitance=47µF voltage=50V package="100 mil [THT, electrolytic]"]
  C2 = Electrolytic Capacitor [capacitance=47µF voltage=50V package="100 mil [THT, electrolytic]"]
  part = Resistor [tolerance=±5% resistance=220 package=THT]
  AMS1117_TO-220 = Voltage Regulator - 3.3V [package="TO220 [THT]"]
  9VDC = Power plug
  Wireless_Transceiver = NRF24L01+ Breakout Board
  AMS1117_SOT-223 = Voltage Regulator - 5V [package="TO220 [THT]"]
  LED1 = LED - 5mm [color="Red (633nm)" package="5 mm [THT]"]
  part_2 = Resistor [tolerance=±5% resistance=220 package=THT]
  LED2 = LED - 5mm [color="Red (633nm)" package="5 mm [THT]"]
  LED3 = LED - 5mm [color="Red (633nm)" package="5 mm [THT]"]
  part_3 = Resistor [tolerance=±5% resistance=220 package=THT]
  part_4 = Resistor [tolerance=±5% resistance=220 package=THT]
  LED4 = LED - 5mm [color="Red (633nm)" package="5 mm [THT]"]
  part_5 = Resistor [tolerance=±5% resistance=220 package=THT]
  LED5 = LED - 5mm [color="Red (633nm)" package="5 mm [THT]"]

nets:
  N1: Microcontroller.D8, part.Pin_1
  N2: Microcontroller.D9_PWM, Wireless_Transceiver.CE
  N3: Microcontroller.D10_PWM/SS, Wireless_Transceiver.CS
  N4: Microcontroller.D11_PWM/MOSI, Wireless_Transceiver.MOSI
  N5: Microcontroller.D12/MISO, Wireless_Transceiver.MISO
  N6: Microcontroller.D13/SCK, Wireless_Transceiver.SCK
  GND: Microcontroller.GND, C1.-, C2.-, AMS1117_TO-220.GND, 9VDC.GND, Wireless_Transceiver.GND, AMS1117_SOT-223.GND, LED1.cathode, LED2.cathode, LED3.cathode, LED4.cathode, LED5.cathode
  N7: Microcontroller.D4, part_5.Pin_1
  N8: Microcontroller.D5_PWM, part_4.Pin_1
  N9: Microcontroller.D6_PWM, part_3.Pin_1
  N10: Microcontroller.D7, part_2.Pin_1
  N11: Microcontroller.5V, C2.+, AMS1117_TO-220.input_voltage, AMS1117_SOT-223.output_voltage
  N12: C1.+, AMS1117_TO-220.output_voltage, Wireless_Transceiver.VCC
  N13: part.Pin_0, LED1.anode
  N14: 9VDC.VCC, AMS1117_SOT-223.input_voltage
  N15: part_2.Pin_0, LED3.anode
  N16: LED2.anode, part_3.Pin_0
  N17: part_4.Pin_0, LED4.anode
  N18: part_5.Pin_0, LED5.anode
