# Fritzing sketch node (saved by Fritzing 0.9.3b)
breadboards: 1

parts:
  Microcontroller = Arduino Uno (Rev3)
  C1 = Electrolytic Capacitor [capacitance=47µF voltage=50V package="100 mil [THT, electrolytic]"]
  C2 = Electrolytic Capacitor [capacitance=47µF voltage=50V package="100 mil [THT, electrolytic]"]
  R2 = Resistor [tolerance=±5% resistance=220 package=THT]
  AMS1117_TO-220 = Voltage Regulator - 3.3V [package="TO220 [THT]"]
  9VDC = Power plug
  Wireless_Transceiver = NRF24L01+ Breakout Board
  LED2 = LED - 5mm [color="Red (633nm)" package="5 mm [THT]"]
  AMS1117_SOT-223 = Voltage Regulator - 5V [package="TO220 [THT]"]
  LED3 = LED - 5mm [color="Red (633nm)" package="5 mm [THT]"]
  R3 = Resistor [tolerance=±5% resistance=220 package=THT]

nets:
  N1: Microcontroller.D9_PWM, Wireless_Transceiver.CE
  N2: Microcontroller.D10_PWM/SS, Wireless_Transceiver.CS
  N3: Microcontroller.D11_PWM/MOSI, Wireless_Transceiver.MOSI
  N4: Microcontroller.D12/MISO, Wireless_Transceiver.MISO
  N5: Microcontroller.D13/SCK, Wireless_Transceiver.SCK
  GND: Microcontroller.GND, C1.-, C2.-, AMS1117_TO-220.GND, 9VDC.GND, Wireless_Transceiver.GND, LED2.cathode, AMS1117_SOT-223.GND, LED3.cathode
  N6: Microcontroller.D5_PWM, R3.Pin_1
  N7: Microcontroller.D6_PWM, R2.Pin_1
  N8: Microcontroller.5V, C2.+, AMS1117_TO-220.input_voltage, AMS1117_SOT-223.output_voltage
  N9: C1.+, AMS1117_TO-220.output_voltage, Wireless_Transceiver.VCC
  N10: R2.Pin_0, LED3.anode
  N11: 9VDC.VCC, AMS1117_SOT-223.input_voltage
  N12: LED2.anode, R3.Pin_0
